# Fritzing sketch thermo-qmtt-dsleep (saved by Fritzing 1.0.1rc)
breadboards: 1

parts:
  A1 = Esp32-c3 super mini
  R1 = Vertical Resistor [tolerance=±5% resistance=120k package=THT]
  R2 = Vertical Resistor [tolerance=±5% resistance=220k package=THT]
  D1 = Schottky Diode [part_number=1N5817 package="300 mil [THT]"]
  V2 = DC Power [voltage=4.2V]

nets:
  N1: A1.Pin_9, R1.Pin_1, R2.Pin_0
  3.3V: A1.Pin_14, R1.Pin_0, D1.cathode
  GND: A1.Pin_15, R2.Pin_1, V2.V-
  N2: D1.anode, V2.V+

notes:
  zf240416.1623

custom parts:
  Esp32-c3 super mini: ESP32-C3 Development Board ESP32 SuperMini Development Board ESP32 Development Board WiFi Bluetooth.
  Vertical Resistor: A generic resistor (0.25W)
